# Fritzing sketch CotexM-Tool_TEST (saved by Fritzing 0.9.2b)
breadboards: 1

parts:
  R1 = Resistor [tolerance=±5% resistance=220 package=THT]
  LED1 = LED - 5mm [color="Red (633nm)" package="5 mm [THT]"]
  U1 = STM32F103 [package=LQFP-48]
  IC1 = Single-Chip USB to UART Bridge [package=mlp28]

nets:
  N1: R1.Pin_0, LED1.anode
  N2: R1.Pin_1, U1.VSS_1, IC1.GND
  N3: LED1.cathode, U1.PA2
  N4: U1.NRST, IC1.DTR
  N5: U1.VDD_2, IC1.VDD
  N6: U1.PA9, IC1.RXD
  N7: U1.PA10, IC1.TXD
  N8: U1.BOOT0, IC1.RTS
